// Digital circuit somador_completro.dig as structural Verilog
module somador_completro (
  input  Cin,
  input  A,
  input  B,
  output S,
  output Cout
);

  wire and_1_out, and_2_out, and_3_out, or_1_out, xor_1_out;

  xor xor_1 (xor_1_out, A, B);
  and and_1 (and_1_out, A, Cin);
  and and_2 (and_2_out, A, B);
  and and_3 (and_3_out, Cin, B);
  xor xor_2 (S, Cin, xor_1_out);
  or or_1 (or_1_out, and_1_out, and_2_out);
  or or_2 (Cout, or_1_out, and_3_out);
endmodule
