// Digital circuit somador_final.dig as structural Verilog
module somador_final (
  input  in_6,
  input  in_7,
  input  in_8,
  input  in_9,
  input  in_10,
  input  in_11,
  input  in_12,
  input  in_13,
  output out_1,
  output out_2,
  output out_3,
  output out_4,
  output out_5
);

  wire comador_completro_1_p5, comador_completro_2_p5, comador_completro_3_p5;

  // comador_completro comador_completro_1: pin names not known; wires that end beside it: 1'b0, in_6, in_10, out_1, comador_completro_1_p5
  // comador_completro comador_completro_2: pin names not known; wires that end beside it: comador_completro_1_p5, in_7, in_11, out_3, comador_completro_2_p5
  // comador_completro comador_completro_3: pin names not known; wires that end beside it: comador_completro_2_p5, in_8, in_12, out_2, comador_completro_3_p5
  // comador_completro comador_completro_4: pin names not known; wires that end beside it: comador_completro_3_p5, in_9, in_13, out_4, out_5
  Seven_Seg_Hex seven_seg_hex_1 (.d({out_4, out_2, out_3, out_1}), .dp(1'b0));
  LED led_1 (.in(out_5));
endmodule
